# Fritzing sketch sensorpack (saved by Fritzing 0.9.3b)
circuit board: 7.8cm x 4.4cm
breadboards: 1

parts:
  RHT1 = Humidity and Temperature Sensor RHT03
  RHT2 = Humidity and Temperature Sensor RHT03
  RHT3 = Humidity and Temperature Sensor RHT03
  RHT4 = Humidity and Temperature Sensor RHT03
  Part1 = Photon
  R4 = Resistor [tolerance=±5% resistance=1k package=THT]
  R3 = Resistor [tolerance=±5% resistance=1k package=THT]
  R2 = Resistor [tolerance=±5% resistance=1k package=THT]
  R1 = Resistor [tolerance=±5% resistance=1k package=THT]
  Breakout_Board1 = Level Shifting uSD Breakout [package="DIP (Dual Inline) [THT]"]

nets:
  VCC: RHT1.Vcc, RHT2.Vcc, RHT3.Vcc, RHT4.Vcc, Part1.VIN, R4.Pin_1, R3.Pin_1, R2.Pin_1, R1.Pin_1, Breakout_Board1.VCC
  N1: RHT1.Data-signal, Part1.D4, R1.Pin_0
  GND: RHT1.GND_2, RHT2.GND_2, RHT3.GND_2, RHT4.GND_2, Part1.GND, Breakout_Board1.GND
  N2: RHT2.Data-signal, Part1.D5, R2.Pin_0
  N3: RHT3.Data-signal, Part1.D6, R3.Pin_0
  N4: RHT4.Data-signal, Part1.D3, R4.Pin_0
  N5: Part1.A2, Breakout_Board1.CS
  N6: Part1.A3, Breakout_Board1.SCK
  N7: Part1.A4, Breakout_Board1.DO
  N8: Part1.A5, Breakout_Board1.DI

notes:
  SASAKI
  SENSOR PCB v2

custom parts:
  Level Shifting uSD Breakout: Breakout board for the TI TXB0104 bi-directional level shifter IC. VccA should be lower than VccB. VccA can range from 1.2V to 3.6V, and VCCB can range from 1.65V to 5.5V.
